# Fritzing sketch shades_ikea (saved by Fritzing 0.9.3b)
breadboards: 1

parts:
  Bauteil1 = Arduino Uno (Rev3)
  KY-2 = Keyes Relay [package=THT]
  KY-3 = Keyes Relay [package=THT]
  KY-4 = Keyes Relay [package=THT]
  S2 = Square Pushbutton
  S3 = Square Pushbutton
  S4 = Square Pushbutton
  S5 = Square Pushbutton
  S6 = Square Pushbutton
  S7 = Square Pushbutton
  Bauteil6 = Ikea 3.3V Tradfri Zigbee Receiver
  Bauteil7 = Ikea 3.3V Tradfri Zigbee Receiver
  Bauteil8 = Ikea 3.3V Tradfri Zigbee Receiver
  KY-5 = Keyes Relay [package=THT]
  KY-6 = Keyes Relay [package=THT]
  KY-7 = Keyes Relay [package=THT]
  M1 = DC Motor
  M2 = DC Motor
  M3 = DC Motor

nets:
  N1: Bauteil1.A0, Bauteil8.OUT
  N2: Bauteil1.A1, Bauteil7.OUT
  N3: Bauteil1.A2, Bauteil6.OUT
  N4: Bauteil1.D8, KY-5.signal
  N5: Bauteil1.D9_PWM, KY-6.signal
  N6: Bauteil1.D10_PWM/SS, KY-7.signal
  N7: Bauteil1.D11_PWM/MOSI, KY-4.signal
  N8: Bauteil1.D12/MISO, KY-3.signal
  N9: Bauteil1.D13/SCK, KY-2.signal
  GND: Bauteil1.GND, KY-2.ground, KY-3.ground, KY-4.ground, Bauteil6.GND, Bauteil7.GND, Bauteil8.GND, KY-5.ground, KY-6.ground, KY-7.ground
  N10: Bauteil1.D2, S7.leg1
  N11: Bauteil1.D3_PWM, S4.leg1
  N12: Bauteil1.D4, S2.leg1
  N13: Bauteil1.D5_PWM, S6.leg1
  N14: Bauteil1.D6_PWM, S5.leg1
  N15: Bauteil1.D7, S3.leg1
  VCC: Bauteil1.3V3, Bauteil6.VCC, Bauteil7.VCC, Bauteil8.VCC
  N16: Bauteil1.5V, KY-2.power, KY-3.power, KY-4.power, S2.leg0, S3.leg0, S4.leg0, S5.leg0, S6.leg0, S7.leg0, KY-5.power, KY-6.power, KY-7.power
  N17: KY-2.C, KY-3.C, KY-4.C
  N18: KY-2.NO, M1.pin_2
  N19: KY-3.NO, M2.pin_2
  N20: KY-4.NO, M3.pin_2
  N21: KY-5.C, KY-6.C, KY-7.C
  N22: KY-5.NO, M3.pin_1
  N23: KY-6.NO, M2.pin_1
  N24: KY-7.NO, M1.pin_1

notes:
  UP DOWN
  Taster Rollo 1
  UP DOWN
  Taster Rollo 2
  UP DOWN
  Taster Rollo 3
  Zigbee Shade3
  Motor UP Relays
  Motor DOWN Relays
  Zigbee Shade2
  Zigbee Shade1
  Motor 1
  Motor 2
  Motor 3
  3.3 V !!!

custom parts:
  Keyes Relay: The Keyes 5V relay module is suitable for SCM development, home appliance control. It uses a 5V~12V TIL control signal which can control DC / AC signal.
  Ikea 3.3V Tradfri Zigbee Receiver: Description: Ikea 3.3V Tradfri Zigbee Receiver Signal is PWM (random 1 and 0) 600 Hz Mighty Gecko-Reihe (EFR32MG1P132GI)

// code stored in the sketch: Untitled2.ino

